// Logisim project adder.circ as structural Verilog: 3 circuits, main circuit main
module main (
  input  [15:0] B,
  input  [15:0] A,
  input  sub,
  output [15:0] result,
  output ovf
);

  wire adds_1_ovf, adds_2_ovf, adds_3_ovf, adds_4_ovf, adds_5_ovf, adds_6_ovf, adds_7_ovf, adds_8_ovf,
       adds_9_ovf, adds_10_ovf, adds_11_ovf, adds_12_ovf, adds_13_ovf, adds_14_ovf, adds_15_ovf, adds_16_ovf,
       xor_2_out, xor_3_out, xor_4_out, xor_5_out, xor_6_out, xor_7_out, xor_8_out, xor_9_out, xor_10_out,
       xor_11_out, xor_12_out, xor_13_out, xor_14_out, xor_15_out, xor_16_out, xor_17_out;

  xor xor_1 (ovf, adds_1_ovf, adds_2_ovf);
  xor xor_2 (xor_2_out, sub, B[15]);
  xor xor_3 (xor_3_out, sub, B[14]);
  adds adds_1 (.result(result[15]), .Cin(adds_2_ovf), .ovf(adds_1_ovf), .B(A[15]), .A(xor_2_out));
  xor xor_4 (xor_4_out, sub, B[13]);
  adds adds_2 (.result(result[14]), .Cin(adds_3_ovf), .ovf(adds_2_ovf), .B(A[14]), .A(xor_3_out));
  adds adds_3 (.result(result[13]), .Cin(adds_5_ovf), .ovf(adds_3_ovf), .B(A[13]), .A(xor_4_out));
  xor xor_5 (xor_5_out, sub, B[12]);
  adds adds_4 (.result(result[11]), .Cin(adds_6_ovf), .ovf(adds_4_ovf), .B(A[11]), .A(xor_6_out));
  adds adds_5 (.result(result[12]), .Cin(adds_4_ovf), .ovf(adds_5_ovf), .B(A[12]), .A(xor_5_out));
  xor xor_6 (xor_6_out, sub, B[11]);
  xor xor_7 (xor_7_out, sub, B[10]);
  adds adds_6 (.result(result[10]), .Cin(adds_8_ovf), .ovf(adds_6_ovf), .B(A[10]), .A(xor_7_out));
  xor xor_8 (xor_8_out, sub, B[9]);
  adds adds_7 (.result(result[8]), .Cin(adds_9_ovf), .ovf(adds_7_ovf), .B(A[8]), .A(xor_9_out));
  adds adds_8 (.result(result[9]), .Cin(adds_7_ovf), .ovf(adds_8_ovf), .B(A[9]), .A(xor_8_out));
  xor xor_9 (xor_9_out, sub, B[8]);
  adds adds_9 (.result(result[7]), .Cin(adds_10_ovf), .ovf(adds_9_ovf), .B(A[7]), .A(xor_10_out));
  xor xor_10 (xor_10_out, sub, B[7]);
  xor xor_11 (xor_11_out, sub, B[6]);
  adds adds_10 (.result(result[6]), .Cin(adds_11_ovf), .ovf(adds_10_ovf), .B(A[6]), .A(xor_11_out));
  adds adds_11 (.result(result[5]), .Cin(adds_13_ovf), .ovf(adds_11_ovf), .B(A[5]), .A(xor_12_out));
  xor xor_12 (xor_12_out, sub, B[5]);
  adds adds_12 (.result(result[3]), .Cin(adds_14_ovf), .ovf(adds_12_ovf), .B(A[3]), .A(xor_15_out));
  adds adds_13 (.result(result[4]), .Cin(adds_12_ovf), .ovf(adds_13_ovf), .B(A[4]), .A(xor_13_out));
  xor xor_13 (xor_13_out, sub, B[4]);
  adds adds_14 (.result(result[2]), .Cin(adds_15_ovf), .ovf(adds_14_ovf), .B(A[2]), .A(xor_14_out));
  xor xor_14 (xor_14_out, sub, B[2]);
  xor xor_15 (xor_15_out, sub, B[3]);
  adds adds_15 (.result(result[1]), .Cin(adds_16_ovf), .ovf(adds_15_ovf), .B(A[1]), .A(xor_16_out));
  adds adds_16 (.result(result[0]), .Cin(sub), .ovf(adds_16_ovf), .B(A[0]), .A(xor_17_out));
  xor xor_16 (xor_16_out, sub, B[1]);
  xor xor_17 (xor_17_out, sub, B[0]);

  // Other names for the same wires on the sheet: B0 = A[0]; B1 = A[1]; B2 = A[2]; B3 = A[3]; B4 = A[4]; B5 = A[5];
  //   B6 = A[6]; B7 = A[7]; B8 = A[8]; B9 = A[9]; B10 = A[10]; B11 = A[11]; B12 = A[12]; B13 = A[13]; B14 = A[14];
  //   B15 = A[15]; A0 = B[0]; A1 = B[1]; A2 = B[2]; A3 = B[3]; A4 = B[4]; A5 = B[5]; A6 = B[6]; A7 = B[7]; A8 = B[8];
  //   A9 = B[9]; A10 = B[10]; A11 = B[11]; A12 = B[12]; A13 = B[13]; A14 = B[14]; A15 = B[15]

  // Notes on the sheet:
  //   THIS CIRCUIT IS A BIT GOOFY AS THE ORIGINAL LAYOUT DOES B-A NOT A-B
  //   TO SOLVE, I JUST FLIPPED THE INPUTS, SO LABELS WILL LOOK OFF
endmodule

module adds (
  input  Cin,
  input  A,
  input  B,
  output result,
  output ovf
);

  wire and_1_out, and_2_out, xor_1_out;

  and and_1 (and_1_out, B, A);
  or or_1 (ovf, and_1_out, and_2_out);
  xor xor_1 (xor_1_out, A, B);
  and and_2 (and_2_out, xor_1_out, Cin);
  xor xor_2 (result, Cin, xor_1_out);
endmodule

module sixteenBitAdder (
  input  [15:0] B,
  input  [15:0] A,
  input  sub,
  output [15:0] result,
  output ovf
);

  wire adds_1_ovf, adds_3_ovf, adds_4_ovf, adds_5_ovf, adds_6_ovf, adds_7_ovf, adds_8_ovf, adds_9_ovf,
       adds_10_ovf, adds_11_ovf, adds_12_ovf, adds_13_ovf, adds_14_ovf, adds_15_ovf, adds_16_ovf,
       adds_17_ovf, xor_2_out, xor_3_out, xor_4_out, xor_5_out, xor_6_out, xor_7_out, xor_8_out, xor_9_out,
       xor_10_out, xor_11_out, xor_12_out, xor_13_out, xor_14_out, xor_15_out, xor_16_out, xor_17_out;

  xor xor_1 (ovf, adds_1_ovf, adds_4_ovf);
  xor xor_2 (xor_2_out, sub, B[14]);
  xor xor_3 (xor_3_out, sub, B[15]);
  adds adds_1 (.result(result[15]), .Cin(adds_4_ovf), .ovf(adds_1_ovf), .B(A[15]), .A(xor_3_out));
  xor xor_4 (xor_4_out, sub, B[13]);
  adds adds_2 ();  // open: result, Cin, ovf, B, A
  adds adds_3 (.result(result[13]), .Cin(adds_6_ovf), .ovf(adds_3_ovf), .B(A[13]), .A(xor_4_out));
  adds adds_4 (.result(result[14]), .Cin(adds_3_ovf), .ovf(adds_4_ovf), .B(A[14]), .A(xor_2_out));
  xor xor_5 (xor_5_out, sub, B[12]);
  adds adds_5 (.result(result[11]), .Cin(adds_7_ovf), .ovf(adds_5_ovf), .B(A[11]), .A(xor_6_out));
  adds adds_6 (.result(result[12]), .Cin(adds_5_ovf), .ovf(adds_6_ovf), .B(A[12]), .A(xor_5_out));
  xor xor_6 (xor_6_out, sub, B[11]);
  xor xor_7 (xor_7_out, sub, B[10]);
  adds adds_7 (.result(result[10]), .Cin(adds_9_ovf), .ovf(adds_7_ovf), .B(A[10]), .A(xor_7_out));
  xor xor_8 (xor_8_out, sub, B[9]);
  adds adds_8 (.result(result[8]), .Cin(adds_10_ovf), .ovf(adds_8_ovf), .B(A[8]), .A(xor_9_out));
  adds adds_9 (.result(result[9]), .Cin(adds_8_ovf), .ovf(adds_9_ovf), .B(A[9]), .A(xor_8_out));
  xor xor_9 (xor_9_out, sub, B[8]);
  adds adds_10 (.result(result[7]), .Cin(adds_11_ovf), .ovf(adds_10_ovf), .B(A[7]), .A(xor_11_out));
  xor xor_10 (xor_10_out, sub, B[6]);
  xor xor_11 (xor_11_out, sub, B[7]);
  adds adds_11 (.result(result[6]), .Cin(adds_12_ovf), .ovf(adds_11_ovf), .B(A[6]), .A(xor_10_out));
  adds adds_12 (.result(result[5]), .Cin(adds_13_ovf), .ovf(adds_12_ovf), .B(A[5]), .A(xor_12_out));
  xor xor_12 (xor_12_out, sub, B[5]);
  adds adds_13 (.result(result[4]), .Cin(adds_14_ovf), .ovf(adds_13_ovf), .B(A[4]), .A(xor_13_out));
  adds adds_14 (.result(result[3]), .Cin(adds_15_ovf), .ovf(adds_14_ovf), .B(A[3]), .A(xor_15_out));
  xor xor_13 (xor_13_out, sub, B[4]);
  adds adds_15 (.result(result[2]), .Cin(adds_17_ovf), .ovf(adds_15_ovf), .B(A[2]), .A(xor_14_out));
  xor xor_14 (xor_14_out, sub, B[2]);
  xor xor_15 (xor_15_out, sub, B[3]);
  adds adds_16 (.result(result[0]), .Cin(sub), .ovf(adds_16_ovf), .B(A[0]), .A(xor_17_out));
  adds adds_17 (.result(result[1]), .Cin(adds_16_ovf), .ovf(adds_17_ovf), .B(A[1]), .A(xor_16_out));
  xor xor_16 (xor_16_out, sub, B[1]);
  xor xor_17 (xor_17_out, sub, B[0]);

  // Other names for the same wires on the sheet: B0 = A[0]; B1 = A[1]; B2 = A[2]; B3 = A[3]; B4 = A[4]; B5 = A[5];
  //   B6 = A[6]; B7 = A[7]; B8 = A[8]; B9 = A[9]; B10 = A[10]; B11 = A[11]; B12 = A[12]; B13 = A[13]; B14 = A[14];
  //   B15 = A[15]; A0 = B[0]; A1 = B[1]; A2 = B[2]; A3 = B[3]; A4 = B[4]; A5 = B[5]; A6 = B[6]; A7 = B[7]; A8 = B[8];
  //   A9 = B[9]; A10 = B[10]; A11 = B[11]; A12 = B[12]; A13 = B[13]; A14 = B[14]; A15 = B[15]

  // Notes on the sheet:
  //   THIS CIRCUIT IS A BIT GOOFY AS THE ORIGINAL LAYOUT DOES B-A NOT A-B
  //   TO SOLVE, I JUST FLIPPED THE INPUTS, SO LABELS WILL LOOK OFF
endmodule
