// Logisim project fsm.circ as structural Verilog: 1 circuit, main circuit main
// in2
module main (
  input  in1,
  input  in2,
  output out
);

  wire and_1_out, and_2_out, and_3_out, and_4_out, and_5_out, and_6_out, clk, notin1, notin2, notQ1, notQ2,
       or_1_out, or_2_out, Q0, Q1;

  and and_1 (and_1_out, Q0, notin1, in2);
  and and_2 (and_2_out, Q0, notin2, in1);
  and and_3 (and_3_out, Q0, notin1, in2);
  and and_4 (and_4_out, notQ1, notin1, in2);
  and and_5 (and_5_out, Q0, notin2, in1);
  and and_6 (and_6_out, notQ1, notin2, in1);
  or or_1 (or_1_out, and_1_out, and_2_out);
  or or_2 (or_2_out, and_3_out, and_4_out, and_5_out, and_6_out);
  D_Flip_Flop u_Q1 (.D(or_1_out), .clk(clk), .Q(Q1), .Qn(notQ1));  // open: preset, reset
  not not_1 (notin1, in1);
  not not_2 (notin2, in2);
  Clock u_clk (.out(clk));
  D_Flip_Flop u_Q0 (.D(or_2_out), .clk(clk), .Q(Q0), .Qn(notQ2));  // open: preset, reset
  and and_7 (out, Q1, Q0);
endmodule
