// Logisim project Vers4ALU_Done.circ as structural Verilog
module Register (
  input  Reset,
  input  clk,
  input  enable,
  input  [15:0] in_4,
  output [15:0] out_5
);

  wire clk_t;

  and and_1 (clk_t, clk, enable);
  D_Flip_Flop d_ff_1 (.D(in_4[0]), .clk(clk_t), .Q(out_5[0]), .reset(Reset));  // open: Qn, preset
  D_Flip_Flop d_ff_2 (.D(in_4[1]), .clk(clk_t), .Q(out_5[1]), .reset(Reset));  // open: Qn, preset
  D_Flip_Flop d_ff_3 (.D(in_4[2]), .clk(clk_t), .Q(out_5[2]), .reset(Reset));  // open: Qn, preset
  D_Flip_Flop d_ff_4 (.D(in_4[3]), .clk(clk_t), .Q(out_5[3]), .reset(Reset));  // open: Qn, preset
  D_Flip_Flop d_ff_5 (.D(in_4[4]), .clk(clk_t), .Q(out_5[4]), .reset(Reset));  // open: Qn, preset
  D_Flip_Flop d_ff_6 (.D(in_4[5]), .clk(clk_t), .Q(out_5[5]), .reset(Reset));  // open: Qn, preset
  D_Flip_Flop d_ff_7 (.D(in_4[6]), .clk(clk_t), .Q(out_5[6]), .reset(Reset));  // open: Qn, preset
  D_Flip_Flop d_ff_8 (.D(in_4[7]), .clk(clk_t), .Q(out_5[7]), .reset(Reset));  // open: Qn, preset
  D_Flip_Flop d_ff_9 (.D(in_4[8]), .clk(clk_t), .Q(out_5[8]), .reset(Reset));  // open: Qn, preset
  D_Flip_Flop d_ff_10 (.D(in_4[9]), .clk(clk_t), .Q(out_5[9]), .reset(Reset));  // open: Qn, preset
  D_Flip_Flop d_ff_11 (.D(in_4[10]), .clk(clk_t), .Q(out_5[10]), .reset(Reset));  // open: Qn, preset
  D_Flip_Flop d_ff_12 (.D(in_4[11]), .clk(clk_t), .Q(out_5[11]), .reset(Reset));  // open: Qn, preset
  D_Flip_Flop d_ff_13 (.D(in_4[12]), .clk(clk_t), .Q(out_5[12]), .reset(Reset));  // open: Qn, preset
  D_Flip_Flop d_ff_14 (.D(in_4[13]), .clk(clk_t), .Q(out_5[13]), .reset(Reset));  // open: Qn, preset
  D_Flip_Flop d_ff_15 (.D(in_4[14]), .clk(clk_t), .Q(out_5[14]), .reset(Reset));  // open: Qn, preset
  D_Flip_Flop d_ff_16 (.D(in_4[15]), .clk(clk_t), .Q(out_5[15]), .reset(Reset));  // open: Qn, preset

  // Other names for the same wires on the sheet: bit0 = in_4[0]; bit1 = in_4[1]; bit2 = in_4[2]; bit3 = in_4[3];
  //   bit4 = in_4[4]; bit5 = in_4[5]; bit6 = in_4[6]; bit7 = in_4[7]; bit8 = in_4[8]; bit9 = in_4[9];
  //   bit10 = in_4[10]; bit11 = in_4[11]; bit12 = in_4[12]; bit13 = in_4[13]; bit14 = in_4[14]; bit15 = in_4[15];
  //   out0 = out_5[0]; out1 = out_5[1]; out2 = out_5[2]; out3 = out_5[3]; out4 = out_5[4]; out5 = out_5[5];
  //   out6 = out_5[6]; out7 = out_5[7]; out8 = out_5[8]; out9 = out_5[9]; out10 = out_5[10]; out11 = out_5[11];
  //   out12 = out_5[12]; out13 = out_5[13]; out14 = out_5[14]; out15 = out_5[15]

  // Notes on the sheet:
  //   Input
  //   Output
endmodule

module ALU (
  input  [15:0] A,
  input  [15:0] B,
  input  [1:0] op,
  output [15:0] out
);

  wire [15:0] add16_1_result, add16_2_result, and_1_out, or_1_out;

  add16 add16_1 (.B(B), .A(A), .sub(1'b0), .result(add16_1_result));  // open: ovf
  add16 add16_2 (.B(B), .A(A), .sub(1'b1), .result(add16_2_result));  // open: ovf
  assign or_1_out = A | B;  // OR_Gate or_1, 16 bits wide
  assign and_1_out = A & B;  // AND_Gate and_1, 16 bits wide
  Multiplexer #(.select(2), .width(16), .enable("false")) multiplexer_1 (
    .in0(or_1_out), .in1(and_1_out), .in2(add16_1_result), .in3(add16_2_result), .out(out), .sel(op));

  // Notes on the sheet:
  //   OR: 00
  //   AND: 01
  //   ADD: 10
  //   SUB: 11
endmodule

module adds (
  input  Cin,
  input  A,
  input  B,
  output result,
  output ovf
);

  wire and_1_out, and_2_out, xor_1_out;

  and and_1 (and_1_out, B, A);
  or or_1 (ovf, and_1_out, and_2_out);
  xor xor_1 (xor_1_out, A, B);
  and and_2 (and_2_out, xor_1_out, Cin);
  xor xor_2 (result, Cin, xor_1_out);
endmodule

module add16 (
  input  [15:0] B,
  input  [15:0] A,
  input  sub,
  output [15:0] result,
  output ovf
);

  wire adds_1_ovf, adds_2_ovf, adds_3_ovf, adds_4_ovf, adds_5_ovf, adds_6_ovf, adds_7_ovf, adds_8_ovf,
       adds_9_ovf, adds_10_ovf, adds_11_ovf, adds_12_ovf, adds_13_ovf, adds_14_ovf, adds_15_ovf, adds_16_ovf,
       xor_2_out, xor_3_out, xor_4_out, xor_5_out, xor_6_out, xor_7_out, xor_8_out, xor_9_out, xor_10_out,
       xor_11_out, xor_12_out, xor_13_out, xor_14_out, xor_15_out, xor_16_out, xor_17_out;

  xor xor_1 (ovf, adds_1_ovf, adds_2_ovf);
  xor xor_2 (xor_2_out, sub, B[15]);
  xor xor_3 (xor_3_out, sub, B[14]);
  adds adds_1 (.A(xor_2_out), .B(A[15]), .result(result[15]), .Cin(adds_2_ovf), .ovf(adds_1_ovf));
  xor xor_4 (xor_4_out, sub, B[13]);
  adds adds_2 (.A(xor_3_out), .B(A[14]), .result(result[14]), .Cin(adds_3_ovf), .ovf(adds_2_ovf));
  adds adds_3 (.A(xor_4_out), .B(A[13]), .result(result[13]), .Cin(adds_4_ovf), .ovf(adds_3_ovf));
  xor xor_5 (xor_5_out, sub, B[12]);
  adds adds_4 (.A(xor_5_out), .B(A[12]), .result(result[12]), .Cin(adds_5_ovf), .ovf(adds_4_ovf));
  adds adds_5 (.A(xor_6_out), .B(A[11]), .result(result[11]), .Cin(adds_6_ovf), .ovf(adds_5_ovf));
  xor xor_6 (xor_6_out, sub, B[11]);
  xor xor_7 (xor_7_out, sub, B[10]);
  adds adds_6 (.A(xor_7_out), .B(A[10]), .result(result[10]), .Cin(adds_8_ovf), .ovf(adds_6_ovf));
  xor xor_8 (xor_8_out, sub, B[9]);
  adds adds_7 (.A(xor_9_out), .B(A[8]), .result(result[8]), .Cin(adds_9_ovf), .ovf(adds_7_ovf));
  adds adds_8 (.A(xor_8_out), .B(A[9]), .result(result[9]), .Cin(adds_7_ovf), .ovf(adds_8_ovf));
  xor xor_9 (xor_9_out, sub, B[8]);
  adds adds_9 (.A(xor_10_out), .B(A[7]), .result(result[7]), .Cin(adds_11_ovf), .ovf(adds_9_ovf));
  xor xor_10 (xor_10_out, sub, B[7]);
  xor xor_11 (xor_11_out, sub, B[6]);
  adds adds_10 (.A(xor_12_out), .B(A[5]), .result(result[5]), .Cin(adds_13_ovf), .ovf(adds_10_ovf));
  adds adds_11 (.A(xor_11_out), .B(A[6]), .result(result[6]), .Cin(adds_10_ovf), .ovf(adds_11_ovf));
  xor xor_12 (xor_12_out, sub, B[5]);
  adds adds_12 (.A(xor_14_out), .B(A[3]), .result(result[3]), .Cin(adds_14_ovf), .ovf(adds_12_ovf));
  adds adds_13 (.A(xor_13_out), .B(A[4]), .result(result[4]), .Cin(adds_12_ovf), .ovf(adds_13_ovf));
  xor xor_13 (xor_13_out, sub, B[4]);
  adds adds_14 (.A(xor_15_out), .B(A[2]), .result(result[2]), .Cin(adds_16_ovf), .ovf(adds_14_ovf));
  xor xor_14 (xor_14_out, sub, B[3]);
  xor xor_15 (xor_15_out, sub, B[2]);
  adds adds_15 (.A(xor_17_out), .B(A[0]), .result(result[0]), .Cin(sub), .ovf(adds_15_ovf));
  adds adds_16 (.A(xor_16_out), .B(A[1]), .result(result[1]), .Cin(adds_15_ovf), .ovf(adds_16_ovf));
  xor xor_16 (xor_16_out, sub, B[1]);
  xor xor_17 (xor_17_out, sub, B[0]);

  // Other names for the same wires on the sheet: B0 = A[0]; B1 = A[1]; B2 = A[2]; B3 = A[3]; B4 = A[4]; B5 = A[5];
  //   B6 = A[6]; B7 = A[7]; B8 = A[8]; B9 = A[9]; B10 = A[10]; B11 = A[11]; B12 = A[12]; B13 = A[13]; B14 = A[14];
  //   B15 = A[15]; A0 = B[0]; A1 = B[1]; A2 = B[2]; A3 = B[3]; A4 = B[4]; A5 = B[5]; A6 = B[6]; A7 = B[7]; A8 = B[8];
  //   A9 = B[9]; A10 = B[10]; A11 = B[11]; A12 = B[12]; A13 = B[13]; A14 = B[14]; A15 = B[15]

  // Notes on the sheet:
  //   THIS CIRCUIT IS A BIT GOOFY AS THE ORIGINAL LAYOUT DOES B-A NOT A-B
  //   TO SOLVE, I JUST FLIPPED THE INPUTS, SO LABELS WILL LOOK OFF
endmodule
