// Logisim project hw4.circ as structural Verilog: 10 circuits, main circuit main
module main (
  input  reset
);

  wire and_1_out, and_2_out, and_3_out, BranchEnable, clk, fourbitequator_1_eq, fourbitequator_2_eq,
       fourbitequator_3_eq, fourbitequator_4_eq, fourbitequator_5_eq, fourbitequator_6_eq,
       fourbitequator_7_eq, fourbitequator_8_eq, fourbitequator_9_eq, fourbitequator_10_eq,
       fourbitequator_11_eq, fourbitequator_12_eq, fourbitequator_13_eq, fourbitequator_14_eq,
       fourbitequator_15_eq, fourbitequator_16_eq, JumpEnable, KeyAvail, KeyRE, memory_latch_1_oe_latched,
       memory_latch_1_we_latched, not_1_out, RamWE, TTYWE, WE;
  wire [1:0] aluOp;
  wire [2:0] rd, rs, rt;
  wire [5:0] controlled_buffer_27_out, controlled_buffer_28_out, controlled_buffer_64_out,
       controlled_buffer_67_out, controlled_buffer_77_out, controlled_buffer_90_out, rom_1_data;
  wire [6:0] KeyOut, TTYIn;
  wire [11:0] JumpTo;
  wire [15:0] add16_1_result, add16_2_result, add16_3_result, aluA, aluB, aluOut, bit_extender_3_out,
       BranchAmt, controlled_buffer_61_out, leftshift_1_out, memory_latch_1_address_latched,
       memory_latch_1_data_in_latched, multiplexer_1_out, multiplexer_2_out, multiplexer_3_out, pc, RamAddr,
       RamInput, RamOut, RegIn, rightshift_1_out, rsOut, rtOut, undriven, xnor_1_out;
  wire [15:6] rom_1_data_2;

  add16 add16_1 (.B(pc), .A(BranchAmt), .result(add16_1_result));  // open: sub, ovf
  Pull_Resistor pull_resistor_1 (.node(RamWE));
  Pull_Resistor pull_resistor_2 (.node(BranchEnable));
  RAM #(.addrWidth(16), .dataWidth(16), .trigger("high"), .databus("bibus")) ram_1 (
    .addr(memory_latch_1_address_latched), .we(memory_latch_1_we_latched), .oe(memory_latch_1_oe_latched),
    .din(memory_latch_1_data_in_latched), .dout(RamOut));
  memory_latch memory_latch_1 (
    .address(RamAddr), .WE(RamWE), .clk(clk), .data_in(RamInput),
    .address_latched(memory_latch_1_address_latched), .WE_latched(memory_latch_1_we_latched),
    .OE_latched(memory_latch_1_oe_latched), .data_in_latched(memory_latch_1_data_in_latched));
  Clock clock_1 (.out(clk));
  add16 add16_2 (.B(16'h1), .A(multiplexer_1_out), .result(add16_2_result));  // open: sub, ovf
  Multiplexer #(.width(16), .enable("false")) multiplexer_1 (
    .in0(pc), .in1(add16_1_result), .out(multiplexer_1_out), .sel(BranchEnable));
  sixteenbitreg sixteenbitreg_1 (.Reset(reset), .clk(clk), .enable(1'b1), .in_4(multiplexer_2_out), .out_5(pc));
  Multiplexer #(.width(16), .enable("false")) multiplexer_2 (
    .in0(add16_2_result), .in1({pc[15:12], JumpTo}), .out(multiplexer_2_out), .sel(JumpEnable));
  Pull_Resistor pull_resistor_3 (.node(JumpEnable));
  assign RamWE = fourbitequator_4_eq ? 1'b1 : 1'bz;  // Controlled_Buffer controlled_buffer_1
  Keyboard keyboard_1 (.clk(clk), .re(KeyRE), .clr(reset), .avail(KeyAvail), .data(KeyOut));
  ROM #(.addrWidth(16), .dataWidth(16)) rom_1 (.addr(pc), .data({rom_1_data_2, rom_1_data}));
  not not_1 (not_1_out, clk);
  not not_2 (not_1_out, clk);
  Pull_Resistor pull_resistor_4 (.node(WE));
  assign rd = fourbitequator_2_eq ? 3'b111 : 3'bz;  // Controlled_Buffer controlled_buffer_2
  assign WE = fourbitequator_2_eq ? 1'b1 : 1'bz;  // Controlled_Buffer controlled_buffer_3
  assign WE = fourbitequator_3_eq ? 1'b1 : 1'bz;  // Controlled_Buffer controlled_buffer_4
  assign RegIn = fourbitequator_3_eq ? RamOut : 16'bz;  // Controlled_Buffer controlled_buffer_5
  assign RamInput = fourbitequator_4_eq ? rtOut : 16'bz;  // Controlled_Buffer controlled_buffer_6
  assign WE = fourbitequator_4_eq ? 1'b0 : 1'bz;  // Controlled_Buffer controlled_buffer_7
  assign BranchEnable = and_2_out ? 1'b1 : 1'bz;  // Controlled_Buffer controlled_buffer_8
  assign BranchEnable = and_3_out ? 1'b1 : 1'bz;  // Controlled_Buffer controlled_buffer_9
  Pull_Resistor pull_resistor_5 (.node(KeyRE));
  ALU alu_1 (.A(aluA), .B(aluB), .out(aluOut), .op(aluOp));
  assign aluOp = fourbitequator_2_eq ? 2'b10 : 2'bz;  // Controlled_Buffer controlled_buffer_10
  assign RegIn = fourbitequator_2_eq ? aluOut : 16'bz;  // Controlled_Buffer controlled_buffer_11
  assign RamAddr = fourbitequator_3_eq ? aluOut : 16'bz;  // Controlled_Buffer controlled_buffer_12
  assign rd = fourbitequator_3_eq ? rom_1_data_2[8:6] : 3'bz;  // Controlled_Buffer controlled_buffer_13
  assign rt = fourbitequator_4_eq ? rom_1_data_2[8:6] : 3'bz;  // Controlled_Buffer controlled_buffer_14
  assign RamWE = fourbitequator_4_eq ? 1'b1 : 1'bz;  // Controlled_Buffer controlled_buffer_15
  and and_1 (and_1_out, xnor_1_out[0], xnor_1_out[1], xnor_1_out[2], xnor_1_out[3], xnor_1_out[4], xnor_1_out[5], xnor_1_out[6], xnor_1_out[7], xnor_1_out[9], xnor_1_out[10], xnor_1_out[11], xnor_1_out[12], xnor_1_out[13], xnor_1_out[14], xnor_1_out[15], xnor_1_out[8]);
  assign WE = fourbitequator_9_eq ? 1'b1 : 1'bz;  // Controlled_Buffer controlled_buffer_16
  assign WE = fourbitequator_10_eq ? 1'b1 : 1'bz;  // Controlled_Buffer controlled_buffer_17
  assign WE = fourbitequator_11_eq ? 1'b1 : 1'bz;  // Controlled_Buffer controlled_buffer_18
  assign WE = fourbitequator_12_eq ? 1'b1 : 1'bz;  // Controlled_Buffer controlled_buffer_19
  assign WE = fourbitequator_13_eq ? 1'b1 : 1'bz;  // Controlled_Buffer controlled_buffer_20
  assign WE = fourbitequator_14_eq ? 1'b1 : 1'bz;  // Controlled_Buffer controlled_buffer_21
  Pull_Resistor pull_resistor_6 (.node(TTYWE));
  RegisterFile registerfile_1 (
    .clk(not_1_out), .WE(WE), .in_3(reset), .InputData(RegIn), .rsOut(rsOut), .rtOut(rtOut), .rd(rd),
    .rs(rs), .rt(rt));
  assign aluB = fourbitequator_2_eq ? 16'h1 : 16'bz;  // Controlled_Buffer controlled_buffer_22
  assign aluA = fourbitequator_2_eq ? pc : 16'bz;  // Controlled_Buffer controlled_buffer_23
  assign aluOp = fourbitequator_3_eq ? 2'b10 : 2'bz;  // Controlled_Buffer controlled_buffer_24
  assign aluOp = fourbitequator_4_eq ? 2'b10 : 2'bz;  // Controlled_Buffer controlled_buffer_25
  assign RamAddr = fourbitequator_4_eq ? aluOut : 16'bz;  // Controlled_Buffer controlled_buffer_26
  and and_2 (and_2_out, fourbitequator_5_eq, and_1_out);
  assign controlled_buffer_27_out = and_2_out ? rom_1_data : 6'bz;  // Controlled_Buffer controlled_buffer_27
  assign BranchAmt = {{10{controlled_buffer_27_out[5]}}, controlled_buffer_27_out};  // Bit_Extender bit_extender_1
  and and_3 (and_3_out, fourbitequator_6_eq, add16_3_result[15]);
  assign controlled_buffer_28_out = and_3_out ? rom_1_data : 6'bz;  // Controlled_Buffer controlled_buffer_28
  assign BranchAmt = {{10{controlled_buffer_28_out[5]}}, controlled_buffer_28_out};  // Bit_Extender bit_extender_2
  assign rd = fourbitequator_9_eq ? rom_1_data[5:3] : 3'bz;  // Controlled_Buffer controlled_buffer_29
  assign RegIn = fourbitequator_9_eq ? aluOut : 16'bz;  // Controlled_Buffer controlled_buffer_30
  assign RegIn = fourbitequator_10_eq ? aluOut : 16'bz;  // Controlled_Buffer controlled_buffer_31
  assign rd = fourbitequator_10_eq ? rom_1_data_2[8:6] : 3'bz;  // Controlled_Buffer controlled_buffer_32
  assign RegIn = fourbitequator_11_eq ? aluOut : 16'bz;  // Controlled_Buffer controlled_buffer_33
  assign rd = fourbitequator_11_eq ? rom_1_data[5:3] : 3'bz;  // Controlled_Buffer controlled_buffer_34
  assign rd = fourbitequator_12_eq ? rom_1_data[5:3] : 3'bz;  // Controlled_Buffer controlled_buffer_35
  assign RegIn = fourbitequator_12_eq ? aluOut : 16'bz;  // Controlled_Buffer controlled_buffer_36
  assign rd = fourbitequator_13_eq ? rom_1_data[5:3] : 3'bz;  // Controlled_Buffer controlled_buffer_37
  assign RegIn = fourbitequator_13_eq ? aluOut : 16'bz;  // Controlled_Buffer controlled_buffer_38
  assign rd = fourbitequator_14_eq ? rom_1_data_2[8:6] : 3'bz;  // Controlled_Buffer controlled_buffer_39
  assign RegIn = fourbitequator_14_eq ? aluOut : 16'bz;  // Controlled_Buffer controlled_buffer_40
  assign bit_extender_3_out = {{9{1'b0}}, KeyOut};  // Bit_Extender bit_extender_3
  assign JumpEnable = fourbitequator_1_eq ? 1'b1 : 1'bz;  // Controlled_Buffer controlled_buffer_41
  assign JumpEnable = fourbitequator_2_eq ? 1'b1 : 1'bz;  // Controlled_Buffer controlled_buffer_42
  assign aluA = fourbitequator_3_eq ? rsOut : 16'bz;  // Controlled_Buffer controlled_buffer_43
  assign RamWE = fourbitequator_3_eq ? 1'b0 : 1'bz;  // Controlled_Buffer controlled_buffer_44
  assign aluA = fourbitequator_4_eq ? rsOut : 16'bz;  // Controlled_Buffer controlled_buffer_45
  assign xnor_1_out = ~(rsOut ^ rtOut);  // XNOR_Gate xnor_1, 16 bits wide
  assign WE = fourbitequator_7_eq ? 1'b1 : 1'bz;  // Controlled_Buffer controlled_buffer_46
  assign WE = fourbitequator_8_eq ? 1'b1 : 1'bz;  // Controlled_Buffer controlled_buffer_47
  assign aluA = fourbitequator_9_eq ? rsOut : 16'bz;  // Controlled_Buffer controlled_buffer_48
  assign aluB = fourbitequator_9_eq ? rtOut : 16'bz;  // Controlled_Buffer controlled_buffer_49
  assign aluA = fourbitequator_10_eq ? rsOut : 16'bz;  // Controlled_Buffer controlled_buffer_50
  assign aluA = fourbitequator_11_eq ? rsOut : 16'bz;  // Controlled_Buffer controlled_buffer_51
  assign aluB = fourbitequator_11_eq ? rtOut : 16'bz;  // Controlled_Buffer controlled_buffer_52
  assign aluA = fourbitequator_12_eq ? rsOut : 16'bz;  // Controlled_Buffer controlled_buffer_53
  assign aluB = fourbitequator_12_eq ? rtOut : 16'bz;  // Controlled_Buffer controlled_buffer_54
  assign aluA = fourbitequator_13_eq ? rsOut : 16'bz;  // Controlled_Buffer controlled_buffer_55
  assign aluB = fourbitequator_13_eq ? rtOut : 16'bz;  // Controlled_Buffer controlled_buffer_56
  assign aluA = fourbitequator_14_eq ? rsOut : 16'bz;  // Controlled_Buffer controlled_buffer_57
  Multiplexer #(.width(16), .enable("false")) multiplexer_3 (
    .in0(undriven), .in1(bit_extender_3_out), .out(multiplexer_3_out), .sel(KeyAvail));
  assign WE = fourbitequator_15_eq ? 1'b1 : 1'bz;  // Controlled_Buffer controlled_buffer_58
  assign RegIn = fourbitequator_15_eq ? multiplexer_3_out : 16'bz;  // Controlled_Buffer controlled_buffer_59
  assign KeyRE = fourbitequator_16_eq ? 1'b1 : 1'bz;  // Controlled_Buffer controlled_buffer_60
  assign controlled_buffer_61_out = fourbitequator_16_eq ? rsOut : 16'bz;  // Controlled_Buffer controlled_buffer_61
  TTY #(.rows(13), .cols(80), .trigger("falling")) tty_1 (.data(TTYIn), .clk(clk), .we(TTYWE), .clr(reset));
  assign JumpTo = fourbitequator_1_eq ? {rom_1_data_2[11:6], rom_1_data} : 12'bz;  // Controlled_Buffer controlled_buffer_62
  assign JumpTo = fourbitequator_2_eq ? {rom_1_data_2[11:6], rom_1_data} : 12'bz;  // Controlled_Buffer controlled_buffer_63
  assign controlled_buffer_64_out = fourbitequator_3_eq ? rom_1_data : 6'bz;  // Controlled_Buffer controlled_buffer_64
  assign rs = fourbitequator_3_eq ? rom_1_data_2[11:9] : 3'bz;  // Controlled_Buffer controlled_buffer_65
  assign aluB = {{10{controlled_buffer_64_out[5]}}, controlled_buffer_64_out};  // Bit_Extender bit_extender_4
  assign rs = fourbitequator_4_eq ? rom_1_data_2[11:9] : 3'bz;  // Controlled_Buffer controlled_buffer_66
  assign controlled_buffer_67_out = fourbitequator_4_eq ? rom_1_data : 6'bz;  // Controlled_Buffer controlled_buffer_67
  assign aluB = {{10{controlled_buffer_67_out[5]}}, controlled_buffer_67_out};  // Bit_Extender bit_extender_5
  assign rt = fourbitequator_5_eq ? rom_1_data_2[8:6] : 3'bz;  // Controlled_Buffer controlled_buffer_68
  assign rt = fourbitequator_6_eq ? rom_1_data_2[8:6] : 3'bz;  // Controlled_Buffer controlled_buffer_69
  add16 add16_3 (.B(rtOut), .A(rsOut), .sub(1'b1), .result(add16_3_result));  // open: ovf
  assign rd = fourbitequator_7_eq ? rom_1_data[5:3] : 3'bz;  // Controlled_Buffer controlled_buffer_70
  assign RegIn = fourbitequator_7_eq ? rightshift_1_out : 16'bz;  // Controlled_Buffer controlled_buffer_71
  assign RegIn = fourbitequator_8_eq ? leftshift_1_out : 16'bz;  // Controlled_Buffer controlled_buffer_72
  assign rd = fourbitequator_8_eq ? rom_1_data[5:3] : 3'bz;  // Controlled_Buffer controlled_buffer_73
  assign rt = fourbitequator_9_eq ? rom_1_data_2[8:6] : 3'bz;  // Controlled_Buffer controlled_buffer_74
  assign aluOp = fourbitequator_9_eq ? 2'b00 : 2'bz;  // Controlled_Buffer controlled_buffer_75
  assign rs = fourbitequator_9_eq ? rom_1_data_2[11:9] : 3'bz;  // Controlled_Buffer controlled_buffer_76
  assign controlled_buffer_77_out = fourbitequator_10_eq ? rom_1_data : 6'bz;  // Controlled_Buffer controlled_buffer_77
  assign rs = fourbitequator_10_eq ? rom_1_data_2[11:9] : 3'bz;  // Controlled_Buffer controlled_buffer_78
  assign aluOp = fourbitequator_10_eq ? 2'b10 : 2'bz;  // Controlled_Buffer controlled_buffer_79
  assign rt = fourbitequator_11_eq ? rom_1_data_2[8:6] : 3'bz;  // Controlled_Buffer controlled_buffer_80
  assign aluOp = fourbitequator_11_eq ? 2'b10 : 2'bz;  // Controlled_Buffer controlled_buffer_81
  assign rs = fourbitequator_11_eq ? rom_1_data_2[11:9] : 3'bz;  // Controlled_Buffer controlled_buffer_82
  assign aluOp = fourbitequator_12_eq ? 2'b01 : 2'bz;  // Controlled_Buffer controlled_buffer_83
  assign rt = fourbitequator_12_eq ? rom_1_data_2[8:6] : 3'bz;  // Controlled_Buffer controlled_buffer_84
  assign rs = fourbitequator_12_eq ? rom_1_data_2[11:9] : 3'bz;  // Controlled_Buffer controlled_buffer_85
  assign aluOp = fourbitequator_13_eq ? 2'b11 : 2'bz;  // Controlled_Buffer controlled_buffer_86
  assign rt = fourbitequator_13_eq ? rom_1_data_2[8:6] : 3'bz;  // Controlled_Buffer controlled_buffer_87
  assign rs = fourbitequator_13_eq ? rom_1_data_2[11:9] : 3'bz;  // Controlled_Buffer controlled_buffer_88
  assign aluOp = fourbitequator_14_eq ? 2'b11 : 2'bz;  // Controlled_Buffer controlled_buffer_89
  assign controlled_buffer_90_out = fourbitequator_14_eq ? rom_1_data : 6'bz;  // Controlled_Buffer controlled_buffer_90
  assign rs = fourbitequator_14_eq ? rom_1_data_2[11:9] : 3'bz;  // Controlled_Buffer controlled_buffer_91
  assign KeyRE = fourbitequator_15_eq ? 1'b0 : 1'bz;  // Controlled_Buffer controlled_buffer_92
  assign TTYWE = fourbitequator_16_eq ? 1'b1 : 1'bz;  // Controlled_Buffer controlled_buffer_93
  Bit_Extender #(.in_width(16), .out_width(7), .\type ("zero")) bit_extender_6 (
    .in(controlled_buffer_61_out), .out(TTYIn));
  fourBitEquator fourbitequator_1 (.A(rom_1_data_2[15:12]), .B(4'b1100), .eq(fourbitequator_1_eq));
  fourBitEquator fourbitequator_2 (.A(rom_1_data_2[15:12]), .B(4'b1101), .eq(fourbitequator_2_eq));
  fourBitEquator fourbitequator_3 (.A(rom_1_data_2[15:12]), .B(4'b0000), .eq(fourbitequator_3_eq));
  fourBitEquator fourbitequator_4 (.A(rom_1_data_2[15:12]), .B(4'b0001), .eq(fourbitequator_4_eq));
  fourBitEquator fourbitequator_5 (.A(rom_1_data_2[15:12]), .B(4'b0010), .eq(fourbitequator_5_eq));
  assign rs = fourbitequator_5_eq ? rom_1_data_2[11:9] : 3'bz;  // Controlled_Buffer controlled_buffer_94
  fourBitEquator fourbitequator_6 (.A(rom_1_data_2[15:12]), .B(4'b0011), .eq(fourbitequator_6_eq));
  assign rs = fourbitequator_6_eq ? rom_1_data_2[11:9] : 3'bz;  // Controlled_Buffer controlled_buffer_95
  fourBitEquator fourbitequator_7 (.A(rom_1_data_2[15:12]), .B(4'b1010), .eq(fourbitequator_7_eq));
  assign rs = fourbitequator_7_eq ? rom_1_data_2[11:9] : 3'bz;  // Controlled_Buffer controlled_buffer_96
  fourBitEquator fourbitequator_8 (.A(rom_1_data_2[15:12]), .B(4'b1011), .eq(fourbitequator_8_eq));
  assign rs = fourbitequator_8_eq ? rom_1_data_2[11:9] : 3'bz;  // Controlled_Buffer controlled_buffer_97
  fourBitEquator fourbitequator_9 (.A(rom_1_data_2[15:12]), .B(4'b0100), .eq(fourbitequator_9_eq));
  fourBitEquator fourbitequator_10 (.A(rom_1_data_2[15:12]), .B(4'b0110), .eq(fourbitequator_10_eq));
  assign aluB = {{10{controlled_buffer_77_out[5]}}, controlled_buffer_77_out};  // Bit_Extender bit_extender_7
  fourBitEquator fourbitequator_11 (.A(rom_1_data_2[15:12]), .B(4'b0111), .eq(fourbitequator_11_eq));
  fourBitEquator fourbitequator_12 (.A(rom_1_data_2[15:12]), .B(4'b0101), .eq(fourbitequator_12_eq));
  fourBitEquator fourbitequator_13 (.A(rom_1_data_2[15:12]), .B(4'b1000), .eq(fourbitequator_13_eq));
  fourBitEquator fourbitequator_14 (.A(rom_1_data_2[15:12]), .B(4'b1001), .eq(fourbitequator_14_eq));
  assign aluB = {{10{controlled_buffer_90_out[5]}}, controlled_buffer_90_out};  // Bit_Extender bit_extender_8
  fourBitEquator fourbitequator_15 (.A(rom_1_data_2[15:12]), .B(4'b1111), .eq(fourbitequator_15_eq));
  assign rd = fourbitequator_15_eq ? rom_1_data[5:3] : 3'bz;  // Controlled_Buffer controlled_buffer_98
  fourBitEquator fourbitequator_16 (.A(rom_1_data_2[15:12]), .B(4'b1110), .eq(fourbitequator_16_eq));
  assign rs = fourbitequator_16_eq ? rom_1_data_2[11:9] : 3'bz;  // Controlled_Buffer controlled_buffer_99
  RightShift rightshift_1 (.In(rsOut), .shamt(rom_1_data[2:0]), .out(rightshift_1_out));
  LeftShift leftshift_1 (.In(rsOut), .shamt(rom_1_data[2:0]), .out(leftshift_1_out));
  Pull_Resistor pull_resistor_7 ();  // open: node

  // Notes on the sheet:
  //   pcOUT
  //   PC Counter
  //   OUT
  //   contents of rom_1 (hex, n*v repeats v):
  //   7000 604f 608c 5298 56b0 46a0 4c68 203f
  //   j
  //   jal
  //   lw
  //   sw
  //   beq
  //   blt
  //   shr
  //   shl
  //   or
  //   addi
  //   add
  //   and
  //   sub
  //   subi
  //   input
  //   output
endmodule

module sixteenbitreg (
  input  Reset,
  input  clk,
  input  enable,
  input  [15:0] in_4,
  output [15:0] out_5
);

  wire clk_t;

  and and_1 (clk_t, clk, enable);
  D_Flip_Flop d_ff_1 (.D(in_4[0]), .clk(clk_t), .Q(out_5[0]), .reset(Reset));  // open: Qn, preset
  D_Flip_Flop d_ff_2 (.D(in_4[1]), .clk(clk_t), .Q(out_5[1]), .reset(Reset));  // open: Qn, preset
  D_Flip_Flop d_ff_3 (.D(in_4[2]), .clk(clk_t), .Q(out_5[2]), .reset(Reset));  // open: Qn, preset
  D_Flip_Flop d_ff_4 (.D(in_4[3]), .clk(clk_t), .Q(out_5[3]), .reset(Reset));  // open: Qn, preset
  D_Flip_Flop d_ff_5 (.D(in_4[4]), .clk(clk_t), .Q(out_5[4]), .reset(Reset));  // open: Qn, preset
  D_Flip_Flop d_ff_6 (.D(in_4[5]), .clk(clk_t), .Q(out_5[5]), .reset(Reset));  // open: Qn, preset
  D_Flip_Flop d_ff_7 (.D(in_4[6]), .clk(clk_t), .Q(out_5[6]), .reset(Reset));  // open: Qn, preset
  D_Flip_Flop d_ff_8 (.D(in_4[7]), .clk(clk_t), .Q(out_5[7]), .reset(Reset));  // open: Qn, preset
  D_Flip_Flop d_ff_9 (.D(in_4[8]), .clk(clk_t), .Q(out_5[8]), .reset(Reset));  // open: Qn, preset
  D_Flip_Flop d_ff_10 (.D(in_4[9]), .clk(clk_t), .Q(out_5[9]), .reset(Reset));  // open: Qn, preset
  D_Flip_Flop d_ff_11 (.D(in_4[10]), .clk(clk_t), .Q(out_5[10]), .reset(Reset));  // open: Qn, preset
  D_Flip_Flop d_ff_12 (.D(in_4[11]), .clk(clk_t), .Q(out_5[11]), .reset(Reset));  // open: Qn, preset
  D_Flip_Flop d_ff_13 (.D(in_4[12]), .clk(clk_t), .Q(out_5[12]), .reset(Reset));  // open: Qn, preset
  D_Flip_Flop d_ff_14 (.D(in_4[13]), .clk(clk_t), .Q(out_5[13]), .reset(Reset));  // open: Qn, preset
  D_Flip_Flop d_ff_15 (.D(in_4[14]), .clk(clk_t), .Q(out_5[14]), .reset(Reset));  // open: Qn, preset
  D_Flip_Flop d_ff_16 (.D(in_4[15]), .clk(clk_t), .Q(out_5[15]), .reset(Reset));  // open: Qn, preset

  // Other names for the same wires on the sheet: bit0 = in_4[0]; bit1 = in_4[1]; bit2 = in_4[2]; bit3 = in_4[3];
  //   bit4 = in_4[4]; bit5 = in_4[5]; bit6 = in_4[6]; bit7 = in_4[7]; bit8 = in_4[8]; bit9 = in_4[9];
  //   bit10 = in_4[10]; bit11 = in_4[11]; bit12 = in_4[12]; bit13 = in_4[13]; bit14 = in_4[14]; bit15 = in_4[15];
  //   out0 = out_5[0]; out1 = out_5[1]; out2 = out_5[2]; out3 = out_5[3]; out4 = out_5[4]; out5 = out_5[5];
  //   out6 = out_5[6]; out7 = out_5[7]; out8 = out_5[8]; out9 = out_5[9]; out10 = out_5[10]; out11 = out_5[11];
  //   out12 = out_5[12]; out13 = out_5[13]; out14 = out_5[14]; out15 = out_5[15]

  // Notes on the sheet:
  //   Input
  //   Output
endmodule

module ALU (
  input  [15:0] A,
  input  [15:0] B,
  input  [1:0] op,
  output [15:0] out
);

  wire [15:0] add16_1_result, add16_2_result, and_1_out, or_1_out;

  add16 add16_1 (.B(B), .A(A), .sub(1'b0), .result(add16_1_result));  // open: ovf
  add16 add16_2 (.B(B), .A(A), .sub(1'b1), .result(add16_2_result));  // open: ovf
  assign or_1_out = A | B;  // OR_Gate or_1, 16 bits wide
  assign and_1_out = A & B;  // AND_Gate and_1, 16 bits wide
  Multiplexer #(.select(2), .width(16), .enable("false")) multiplexer_1 (
    .in0(or_1_out), .in1(and_1_out), .in2(add16_1_result), .in3(add16_2_result), .out(out), .sel(op));

  // Notes on the sheet:
  //   OR: 00
  //   AND: 01
  //   ADD: 10
  //   SUB: 11
endmodule

module adds (
  input  Cin,
  input  A,
  input  B,
  output result,
  output ovf
);

  wire and_1_out, and_2_out, xor_1_out;

  and and_1 (and_1_out, B, A);
  or or_1 (ovf, and_1_out, and_2_out);
  xor xor_1 (xor_1_out, A, B);
  and and_2 (and_2_out, xor_1_out, Cin);
  xor xor_2 (result, Cin, xor_1_out);
endmodule

module add16 (
  input  [15:0] B,
  input  [15:0] A,
  input  sub,
  output [15:0] result,
  output ovf
);

  wire adds_1_ovf, adds_2_ovf, adds_3_ovf, adds_4_ovf, adds_5_ovf, adds_6_ovf, adds_7_ovf, adds_8_ovf,
       adds_9_ovf, adds_10_ovf, adds_11_ovf, adds_12_ovf, adds_13_ovf, adds_14_ovf, adds_15_ovf, adds_16_ovf,
       xor_2_out, xor_3_out, xor_4_out, xor_5_out, xor_6_out, xor_7_out, xor_8_out, xor_9_out, xor_10_out,
       xor_11_out, xor_12_out, xor_13_out, xor_14_out, xor_15_out, xor_16_out, xor_17_out;

  xor xor_1 (ovf, adds_1_ovf, adds_2_ovf);
  xor xor_2 (xor_2_out, sub, B[15]);
  xor xor_3 (xor_3_out, sub, B[14]);
  adds adds_1 (.A(xor_2_out), .B(A[15]), .result(result[15]), .Cin(adds_2_ovf), .ovf(adds_1_ovf));
  xor xor_4 (xor_4_out, sub, B[13]);
  adds adds_2 (.A(xor_3_out), .B(A[14]), .result(result[14]), .Cin(adds_3_ovf), .ovf(adds_2_ovf));
  adds adds_3 (.A(xor_4_out), .B(A[13]), .result(result[13]), .Cin(adds_4_ovf), .ovf(adds_3_ovf));
  xor xor_5 (xor_5_out, sub, B[12]);
  adds adds_4 (.A(xor_5_out), .B(A[12]), .result(result[12]), .Cin(adds_5_ovf), .ovf(adds_4_ovf));
  adds adds_5 (.A(xor_7_out), .B(A[11]), .result(result[11]), .Cin(adds_6_ovf), .ovf(adds_5_ovf));
  xor xor_6 (xor_6_out, sub, B[10]);
  xor xor_7 (xor_7_out, sub, B[11]);
  adds adds_6 (.A(xor_6_out), .B(A[10]), .result(result[10]), .Cin(adds_8_ovf), .ovf(adds_6_ovf));
  xor xor_8 (xor_8_out, sub, B[9]);
  adds adds_7 (.A(xor_9_out), .B(A[8]), .result(result[8]), .Cin(adds_9_ovf), .ovf(adds_7_ovf));
  adds adds_8 (.A(xor_8_out), .B(A[9]), .result(result[9]), .Cin(adds_7_ovf), .ovf(adds_8_ovf));
  xor xor_9 (xor_9_out, sub, B[8]);
  adds adds_9 (.A(xor_10_out), .B(A[7]), .result(result[7]), .Cin(adds_10_ovf), .ovf(adds_9_ovf));
  xor xor_10 (xor_10_out, sub, B[7]);
  xor xor_11 (xor_11_out, sub, B[6]);
  adds adds_10 (.A(xor_11_out), .B(A[6]), .result(result[6]), .Cin(adds_11_ovf), .ovf(adds_10_ovf));
  adds adds_11 (.A(xor_12_out), .B(A[5]), .result(result[5]), .Cin(adds_13_ovf), .ovf(adds_11_ovf));
  xor xor_12 (xor_12_out, sub, B[5]);
  adds adds_12 (.A(xor_15_out), .B(A[3]), .result(result[3]), .Cin(adds_14_ovf), .ovf(adds_12_ovf));
  adds adds_13 (.A(xor_13_out), .B(A[4]), .result(result[4]), .Cin(adds_12_ovf), .ovf(adds_13_ovf));
  xor xor_13 (xor_13_out, sub, B[4]);
  adds adds_14 (.A(xor_14_out), .B(A[2]), .result(result[2]), .Cin(adds_16_ovf), .ovf(adds_14_ovf));
  xor xor_14 (xor_14_out, sub, B[2]);
  xor xor_15 (xor_15_out, sub, B[3]);
  adds adds_15 (.A(xor_17_out), .B(A[0]), .result(result[0]), .Cin(sub), .ovf(adds_15_ovf));
  adds adds_16 (.A(xor_16_out), .B(A[1]), .result(result[1]), .Cin(adds_15_ovf), .ovf(adds_16_ovf));
  xor xor_16 (xor_16_out, sub, B[1]);
  xor xor_17 (xor_17_out, sub, B[0]);

  // Other names for the same wires on the sheet: B0 = A[0]; B1 = A[1]; B2 = A[2]; B3 = A[3]; B4 = A[4]; B5 = A[5];
  //   B6 = A[6]; B7 = A[7]; B8 = A[8]; B9 = A[9]; B10 = A[10]; B11 = A[11]; B12 = A[12]; B13 = A[13]; B14 = A[14];
  //   B15 = A[15]; A0 = B[0]; A1 = B[1]; A2 = B[2]; A3 = B[3]; A4 = B[4]; A5 = B[5]; A6 = B[6]; A7 = B[7]; A8 = B[8];
  //   A9 = B[9]; A10 = B[10]; A11 = B[11]; A12 = B[12]; A13 = B[13]; A14 = B[14]; A15 = B[15]

  // Notes on the sheet:
  //   THIS CIRCUIT IS A BIT GOOFY AS THE ORIGINAL LAYOUT DOES B-A NOT A-B
  //   TO SOLVE, I JUST FLIPPED THE INPUTS, SO LABELS WILL LOOK OFF
endmodule

module LeftShift (
  input  [15:0] In,
  input  [2:0] shamt,
  output [15:0] out
);

  wire multiplexer_1_out, multiplexer_2_out, multiplexer_4_out, multiplexer_5_out, multiplexer_7_out,
       multiplexer_8_out, multiplexer_9_out, multiplexer_10_out, multiplexer_13_out, multiplexer_14_out,
       multiplexer_16_out, multiplexer_17_out, multiplexer_18_out, multiplexer_19_out, multiplexer_22_out,
       multiplexer_23_out, multiplexer_24_out, multiplexer_25_out, multiplexer_28_out, multiplexer_29_out,
       multiplexer_31_out, multiplexer_32_out, multiplexer_33_out, multiplexer_34_out, multiplexer_37_out,
       multiplexer_38_out, multiplexer_40_out, multiplexer_41_out, multiplexer_42_out, multiplexer_43_out,
       multiplexer_46_out, multiplexer_47_out;

  Multiplexer #(.enable("false")) multiplexer_1 (.in0(In[15]), .in1(In[14]), .out(multiplexer_1_out), .sel(shamt[0]));
  Multiplexer #(.enable("false")) multiplexer_2 (
    .in0(multiplexer_1_out), .in1(multiplexer_7_out), .out(multiplexer_2_out), .sel(shamt[1]));
  Multiplexer #(.enable("false")) multiplexer_3 (
    .in0(multiplexer_2_out), .in1(multiplexer_14_out), .out(out[15]), .sel(shamt[2]));
  Multiplexer #(.enable("false")) multiplexer_4 (.in0(In[14]), .in1(In[13]), .out(multiplexer_4_out), .sel(shamt[0]));
  Multiplexer #(.enable("false")) multiplexer_5 (
    .in0(multiplexer_4_out), .in1(multiplexer_8_out), .out(multiplexer_5_out), .sel(shamt[1]));
  Multiplexer #(.enable("false")) multiplexer_6 (
    .in0(multiplexer_5_out), .in1(multiplexer_18_out), .out(out[14]), .sel(shamt[2]));
  Multiplexer #(.enable("false")) multiplexer_7 (.in0(In[13]), .in1(In[12]), .out(multiplexer_7_out), .sel(shamt[0]));
  Multiplexer #(.enable("false")) multiplexer_8 (.in0(In[12]), .in1(In[11]), .out(multiplexer_8_out), .sel(shamt[0]));
  Multiplexer #(.enable("false")) multiplexer_9 (
    .in0(multiplexer_7_out), .in1(multiplexer_13_out), .out(multiplexer_9_out), .sel(shamt[1]));
  Multiplexer #(.enable("false")) multiplexer_10 (
    .in0(multiplexer_8_out), .in1(multiplexer_16_out), .out(multiplexer_10_out), .sel(shamt[1]));
  Multiplexer #(.enable("false")) multiplexer_11 (
    .in0(multiplexer_10_out), .in1(multiplexer_24_out), .out(out[12]), .sel(shamt[2]));
  Multiplexer #(.enable("false")) multiplexer_12 (
    .in0(multiplexer_9_out), .in1(multiplexer_19_out), .out(out[13]), .sel(shamt[2]));
  Multiplexer #(.enable("false")) multiplexer_13 (.in0(In[11]), .in1(In[10]), .out(multiplexer_13_out), .sel(shamt[0]));
  Multiplexer #(.enable("false")) multiplexer_14 (
    .in0(multiplexer_13_out), .in1(multiplexer_17_out), .out(multiplexer_14_out), .sel(shamt[1]));
  Multiplexer #(.enable("false")) multiplexer_15 (
    .in0(multiplexer_14_out), .in1(multiplexer_25_out), .out(out[11]), .sel(shamt[2]));
  Multiplexer #(.enable("false")) multiplexer_16 (.in0(In[10]), .in1(In[9]), .out(multiplexer_16_out), .sel(shamt[0]));
  Multiplexer #(.enable("false")) multiplexer_17 (.in0(In[9]), .in1(In[8]), .out(multiplexer_17_out), .sel(shamt[0]));
  Multiplexer #(.enable("false")) multiplexer_18 (
    .in0(multiplexer_16_out), .in1(multiplexer_23_out), .out(multiplexer_18_out), .sel(shamt[1]));
  Multiplexer #(.enable("false")) multiplexer_19 (
    .in0(multiplexer_17_out), .in1(multiplexer_22_out), .out(multiplexer_19_out), .sel(shamt[1]));
  Multiplexer #(.enable("false")) multiplexer_20 (
    .in0(multiplexer_18_out), .in1(multiplexer_29_out), .out(out[10]), .sel(shamt[2]));
  Multiplexer #(.enable("false")) multiplexer_21 (
    .in0(multiplexer_19_out), .in1(multiplexer_34_out), .out(out[9]), .sel(shamt[2]));
  Multiplexer #(.enable("false")) multiplexer_22 (.in0(In[7]), .in1(In[6]), .out(multiplexer_22_out), .sel(shamt[0]));
  Multiplexer #(.enable("false")) multiplexer_23 (.in0(In[8]), .in1(In[7]), .out(multiplexer_23_out), .sel(shamt[0]));
  Multiplexer #(.enable("false")) multiplexer_24 (
    .in0(multiplexer_23_out), .in1(multiplexer_28_out), .out(multiplexer_24_out), .sel(shamt[1]));
  Multiplexer #(.enable("false")) multiplexer_25 (
    .in0(multiplexer_22_out), .in1(multiplexer_31_out), .out(multiplexer_25_out), .sel(shamt[1]));
  Multiplexer #(.enable("false")) multiplexer_26 (
    .in0(multiplexer_24_out), .in1(multiplexer_33_out), .out(out[8]), .sel(shamt[2]));
  Multiplexer #(.enable("false")) multiplexer_27 (
    .in0(multiplexer_25_out), .in1(multiplexer_38_out), .out(out[7]), .sel(shamt[2]));
  Multiplexer #(.enable("false")) multiplexer_28 (.in0(In[6]), .in1(In[5]), .out(multiplexer_28_out), .sel(shamt[0]));
  Multiplexer #(.enable("false")) multiplexer_29 (
    .in0(multiplexer_28_out), .in1(multiplexer_32_out), .out(multiplexer_29_out), .sel(shamt[1]));
  Multiplexer #(.enable("false")) multiplexer_30 (
    .in0(multiplexer_29_out), .in1(multiplexer_43_out), .out(out[6]), .sel(shamt[2]));
  Multiplexer #(.enable("false")) multiplexer_31 (.in0(In[5]), .in1(In[4]), .out(multiplexer_31_out), .sel(shamt[0]));
  Multiplexer #(.enable("false")) multiplexer_32 (.in0(In[4]), .in1(In[3]), .out(multiplexer_32_out), .sel(shamt[0]));
  Multiplexer #(.enable("false")) multiplexer_33 (
    .in0(multiplexer_32_out), .in1(multiplexer_41_out), .out(multiplexer_33_out), .sel(shamt[1]));
  Multiplexer #(.enable("false")) multiplexer_34 (
    .in0(multiplexer_31_out), .in1(multiplexer_37_out), .out(multiplexer_34_out), .sel(shamt[1]));
  Multiplexer #(.enable("false")) multiplexer_35 (
    .in0(multiplexer_33_out), .in1(multiplexer_47_out), .out(out[4]), .sel(shamt[2]));
  Multiplexer #(.enable("false")) multiplexer_36 (
    .in0(multiplexer_34_out), .in1(multiplexer_42_out), .out(out[5]), .sel(shamt[2]));
  Multiplexer #(.enable("false")) multiplexer_37 (.in0(In[3]), .in1(In[2]), .out(multiplexer_37_out), .sel(shamt[0]));
  Multiplexer #(.enable("false")) multiplexer_38 (
    .in0(multiplexer_37_out), .in1(multiplexer_40_out), .out(multiplexer_38_out), .sel(shamt[1]));
  Multiplexer #(.enable("false")) multiplexer_39 (.in0(multiplexer_38_out), .in1(1'b0), .out(out[3]), .sel(shamt[2]));
  Multiplexer #(.enable("false")) multiplexer_40 (.in0(In[1]), .in1(In[0]), .out(multiplexer_40_out), .sel(shamt[0]));
  Multiplexer #(.enable("false")) multiplexer_41 (.in0(In[2]), .in1(In[1]), .out(multiplexer_41_out), .sel(shamt[0]));
  Multiplexer #(.enable("false")) multiplexer_42 (
    .in0(multiplexer_40_out), .in1(1'b0), .out(multiplexer_42_out), .sel(shamt[1]));
  Multiplexer #(.enable("false")) multiplexer_43 (
    .in0(multiplexer_41_out), .in1(multiplexer_46_out), .out(multiplexer_43_out), .sel(shamt[1]));
  Multiplexer #(.enable("false")) multiplexer_44 (.in0(multiplexer_42_out), .in1(1'b0), .out(out[1]), .sel(shamt[2]));
  Multiplexer #(.enable("false")) multiplexer_45 (.in0(multiplexer_43_out), .in1(1'b0), .out(out[2]), .sel(shamt[2]));
  Multiplexer #(.enable("false")) multiplexer_46 (.in0(In[0]), .in1(1'b0), .out(multiplexer_46_out), .sel(shamt[0]));
  Multiplexer #(.enable("false")) multiplexer_47 (
    .in0(multiplexer_46_out), .in1(1'b0), .out(multiplexer_47_out), .sel(shamt[1]));
  Multiplexer #(.enable("false")) multiplexer_48 (.in0(multiplexer_47_out), .in1(1'b0), .out(out[0]), .sel(shamt[2]));
endmodule

module RightShift (
  input  [15:0] In,
  input  [2:0] shamt,
  output [15:0] out
);

  wire multiplexer_1_out, multiplexer_2_out, multiplexer_3_out, multiplexer_4_out, multiplexer_7_out,
       multiplexer_8_out, multiplexer_10_out, multiplexer_11_out, multiplexer_12_out, multiplexer_13_out,
       multiplexer_16_out, multiplexer_17_out, multiplexer_18_out, multiplexer_19_out, multiplexer_22_out,
       multiplexer_23_out, multiplexer_25_out, multiplexer_26_out, multiplexer_27_out, multiplexer_28_out,
       multiplexer_31_out, multiplexer_32_out, multiplexer_34_out, multiplexer_35_out, multiplexer_36_out,
       multiplexer_37_out, multiplexer_40_out, multiplexer_41_out, multiplexer_42_out, multiplexer_43_out,
       multiplexer_46_out, multiplexer_47_out;

  Multiplexer #(.enable("false")) multiplexer_1 (.in0(In[0]), .in1(In[1]), .out(multiplexer_1_out), .sel(shamt[0]));
  Multiplexer #(.enable("false")) multiplexer_2 (.in0(In[1]), .in1(In[2]), .out(multiplexer_2_out), .sel(shamt[0]));
  Multiplexer #(.enable("false")) multiplexer_3 (
    .in0(multiplexer_1_out), .in1(multiplexer_7_out), .out(multiplexer_3_out), .sel(shamt[1]));
  Multiplexer #(.enable("false")) multiplexer_4 (
    .in0(multiplexer_2_out), .in1(multiplexer_10_out), .out(multiplexer_4_out), .sel(shamt[1]));
  Multiplexer #(.enable("false")) multiplexer_5 (
    .in0(multiplexer_3_out), .in1(multiplexer_12_out), .out(out[0]), .sel(shamt[2]));
  Multiplexer #(.enable("false")) multiplexer_6 (
    .in0(multiplexer_4_out), .in1(multiplexer_19_out), .out(out[1]), .sel(shamt[2]));
  Multiplexer #(.enable("false")) multiplexer_7 (.in0(In[2]), .in1(In[3]), .out(multiplexer_7_out), .sel(shamt[0]));
  Multiplexer #(.enable("false")) multiplexer_8 (
    .in0(multiplexer_7_out), .in1(multiplexer_11_out), .out(multiplexer_8_out), .sel(shamt[1]));
  Multiplexer #(.enable("false")) multiplexer_9 (
    .in0(multiplexer_8_out), .in1(multiplexer_18_out), .out(out[2]), .sel(shamt[2]));
  Multiplexer #(.enable("false")) multiplexer_10 (.in0(In[3]), .in1(In[4]), .out(multiplexer_10_out), .sel(shamt[0]));
  Multiplexer #(.enable("false")) multiplexer_11 (.in0(In[4]), .in1(In[5]), .out(multiplexer_11_out), .sel(shamt[0]));
  Multiplexer #(.enable("false")) multiplexer_12 (
    .in0(multiplexer_11_out), .in1(multiplexer_17_out), .out(multiplexer_12_out), .sel(shamt[1]));
  Multiplexer #(.enable("false")) multiplexer_13 (
    .in0(multiplexer_10_out), .in1(multiplexer_16_out), .out(multiplexer_13_out), .sel(shamt[1]));
  Multiplexer #(.enable("false")) multiplexer_14 (
    .in0(multiplexer_13_out), .in1(multiplexer_23_out), .out(out[3]), .sel(shamt[2]));
  Multiplexer #(.enable("false")) multiplexer_15 (
    .in0(multiplexer_12_out), .in1(multiplexer_27_out), .out(out[4]), .sel(shamt[2]));
  Multiplexer #(.enable("false")) multiplexer_16 (.in0(In[5]), .in1(In[6]), .out(multiplexer_16_out), .sel(shamt[0]));
  Multiplexer #(.enable("false")) multiplexer_17 (.in0(In[6]), .in1(In[7]), .out(multiplexer_17_out), .sel(shamt[0]));
  Multiplexer #(.enable("false")) multiplexer_18 (
    .in0(multiplexer_17_out), .in1(multiplexer_26_out), .out(multiplexer_18_out), .sel(shamt[1]));
  Multiplexer #(.enable("false")) multiplexer_19 (
    .in0(multiplexer_16_out), .in1(multiplexer_22_out), .out(multiplexer_19_out), .sel(shamt[1]));
  Multiplexer #(.enable("false")) multiplexer_20 (
    .in0(multiplexer_18_out), .in1(multiplexer_32_out), .out(out[6]), .sel(shamt[2]));
  Multiplexer #(.enable("false")) multiplexer_21 (
    .in0(multiplexer_19_out), .in1(multiplexer_28_out), .out(out[5]), .sel(shamt[2]));
  Multiplexer #(.enable("false")) multiplexer_22 (.in0(In[7]), .in1(In[8]), .out(multiplexer_22_out), .sel(shamt[0]));
  Multiplexer #(.enable("false")) multiplexer_23 (
    .in0(multiplexer_22_out), .in1(multiplexer_25_out), .out(multiplexer_23_out), .sel(shamt[1]));
  Multiplexer #(.enable("false")) multiplexer_24 (
    .in0(multiplexer_23_out), .in1(multiplexer_36_out), .out(out[7]), .sel(shamt[2]));
  Multiplexer #(.enable("false")) multiplexer_25 (.in0(In[9]), .in1(In[10]), .out(multiplexer_25_out), .sel(shamt[0]));
  Multiplexer #(.enable("false")) multiplexer_26 (.in0(In[8]), .in1(In[9]), .out(multiplexer_26_out), .sel(shamt[0]));
  Multiplexer #(.enable("false")) multiplexer_27 (
    .in0(multiplexer_26_out), .in1(multiplexer_31_out), .out(multiplexer_27_out), .sel(shamt[1]));
  Multiplexer #(.enable("false")) multiplexer_28 (
    .in0(multiplexer_25_out), .in1(multiplexer_35_out), .out(multiplexer_28_out), .sel(shamt[1]));
  Multiplexer #(.enable("false")) multiplexer_29 (
    .in0(multiplexer_28_out), .in1(multiplexer_42_out), .out(out[9]), .sel(shamt[2]));
  Multiplexer #(.enable("false")) multiplexer_30 (
    .in0(multiplexer_27_out), .in1(multiplexer_37_out), .out(out[8]), .sel(shamt[2]));
  Multiplexer #(.enable("false")) multiplexer_31 (.in0(In[10]), .in1(In[11]), .out(multiplexer_31_out), .sel(shamt[0]));
  Multiplexer #(.enable("false")) multiplexer_32 (
    .in0(multiplexer_31_out), .in1(multiplexer_34_out), .out(multiplexer_32_out), .sel(shamt[1]));
  Multiplexer #(.enable("false")) multiplexer_33 (
    .in0(multiplexer_32_out), .in1(multiplexer_43_out), .out(out[10]), .sel(shamt[2]));
  Multiplexer #(.enable("false")) multiplexer_34 (.in0(In[12]), .in1(In[13]), .out(multiplexer_34_out), .sel(shamt[0]));
  Multiplexer #(.enable("false")) multiplexer_35 (.in0(In[11]), .in1(In[12]), .out(multiplexer_35_out), .sel(shamt[0]));
  Multiplexer #(.enable("false")) multiplexer_36 (
    .in0(multiplexer_35_out), .in1(multiplexer_41_out), .out(multiplexer_36_out), .sel(shamt[1]));
  Multiplexer #(.enable("false")) multiplexer_37 (
    .in0(multiplexer_34_out), .in1(multiplexer_40_out), .out(multiplexer_37_out), .sel(shamt[1]));
  Multiplexer #(.enable("false")) multiplexer_38 (.in0(multiplexer_37_out), .in1(1'b0), .out(out[12]), .sel(shamt[2]));
  Multiplexer #(.enable("false")) multiplexer_39 (
    .in0(multiplexer_36_out), .in1(multiplexer_47_out), .out(out[11]), .sel(shamt[2]));
  Multiplexer #(.enable("false")) multiplexer_40 (.in0(In[14]), .in1(In[15]), .out(multiplexer_40_out), .sel(shamt[0]));
  Multiplexer #(.enable("false")) multiplexer_41 (.in0(In[13]), .in1(In[14]), .out(multiplexer_41_out), .sel(shamt[0]));
  Multiplexer #(.enable("false")) multiplexer_42 (
    .in0(multiplexer_41_out), .in1(multiplexer_46_out), .out(multiplexer_42_out), .sel(shamt[1]));
  Multiplexer #(.enable("false")) multiplexer_43 (
    .in0(multiplexer_40_out), .in1(1'b0), .out(multiplexer_43_out), .sel(shamt[1]));
  Multiplexer #(.enable("false")) multiplexer_44 (.in0(multiplexer_43_out), .in1(1'b0), .out(out[14]), .sel(shamt[2]));
  Multiplexer #(.enable("false")) multiplexer_45 (.in0(multiplexer_42_out), .in1(1'b0), .out(out[13]), .sel(shamt[2]));
  Multiplexer #(.enable("false")) multiplexer_46 (.in0(In[15]), .in1(1'b0), .out(multiplexer_46_out), .sel(shamt[0]));
  Multiplexer #(.enable("false")) multiplexer_47 (
    .in0(multiplexer_46_out), .in1(1'b0), .out(multiplexer_47_out), .sel(shamt[1]));
  Multiplexer #(.enable("false")) multiplexer_48 (.in0(multiplexer_47_out), .in1(1'b0), .out(out[15]), .sel(shamt[2]));
endmodule

module RegisterFile (
  input  clk,
  input  WE,
  input  in_3,
  input  [15:0] InputData,
  input  [2:0] rs,
  input  [2:0] rd,
  input  [2:0] rt,
  output [15:0] rsOut,
  output [15:0] rtOut
);

  wire clk_t, demultiplexer_1_out0, demultiplexer_1_out1, demultiplexer_1_out2, demultiplexer_1_out3,
       demultiplexer_1_out4, demultiplexer_1_out5, demultiplexer_1_out6, demultiplexer_1_out7;
  wire [15:0] sixteenbitreg_1_out_5, sixteenbitreg_2_out_5, sixteenbitreg_3_out_5, sixteenbitreg_4_out_5,
       sixteenbitreg_5_out_5, sixteenbitreg_6_out_5, sixteenbitreg_7_out_5, sixteenbitreg_8_out_5;

  and and_1 (clk_t, clk, WE);
  Demultiplexer #(.select(3), .enable("false")) demultiplexer_1 (
    .out0(demultiplexer_1_out0), .out1(demultiplexer_1_out1), .out2(demultiplexer_1_out2),
    .out3(demultiplexer_1_out3), .out4(demultiplexer_1_out4), .out5(demultiplexer_1_out5),
    .out6(demultiplexer_1_out6), .out7(demultiplexer_1_out7), .in(1'b1), .sel(rd));
  sixteenbitreg sixteenbitreg_1 (
    .Reset(in_3), .clk(clk_t), .in_4(InputData), .out_5(sixteenbitreg_1_out_5));  // open: enable
  sixteenbitreg sixteenbitreg_2 (
    .Reset(in_3), .clk(clk_t), .enable(demultiplexer_1_out1), .in_4(InputData), .out_5(sixteenbitreg_2_out_5));
  sixteenbitreg sixteenbitreg_3 (
    .Reset(in_3), .clk(clk_t), .enable(demultiplexer_1_out2), .in_4(InputData), .out_5(sixteenbitreg_3_out_5));
  sixteenbitreg sixteenbitreg_4 (
    .Reset(in_3), .clk(clk_t), .enable(demultiplexer_1_out3), .in_4(InputData), .out_5(sixteenbitreg_4_out_5));
  sixteenbitreg sixteenbitreg_5 (
    .Reset(in_3), .clk(clk_t), .enable(demultiplexer_1_out4), .in_4(InputData), .out_5(sixteenbitreg_5_out_5));
  sixteenbitreg sixteenbitreg_6 (
    .Reset(in_3), .clk(clk_t), .enable(demultiplexer_1_out5), .in_4(InputData), .out_5(sixteenbitreg_6_out_5));
  sixteenbitreg sixteenbitreg_7 (
    .Reset(in_3), .clk(clk_t), .enable(demultiplexer_1_out6), .in_4(InputData), .out_5(sixteenbitreg_7_out_5));
  sixteenbitreg sixteenbitreg_8 (
    .Reset(in_3), .clk(clk_t), .enable(demultiplexer_1_out7), .in_4(InputData), .out_5(sixteenbitreg_8_out_5));
  // Probe on sixteenbitreg_1_out_5
  // Probe on sixteenbitreg_2_out_5
  // Probe on sixteenbitreg_3_out_5
  // Probe on sixteenbitreg_4_out_5
  // Probe on sixteenbitreg_5_out_5
  // Probe on sixteenbitreg_6_out_5
  // Probe on sixteenbitreg_7_out_5
  // Probe on sixteenbitreg_8_out_5
  Multiplexer #(.select(3), .width(16), .enable("false")) multiplexer_1 (
    .in0(sixteenbitreg_1_out_5), .in1(sixteenbitreg_2_out_5), .in2(sixteenbitreg_3_out_5),
    .in3(sixteenbitreg_4_out_5), .in4(sixteenbitreg_5_out_5), .in5(sixteenbitreg_6_out_5),
    .in6(sixteenbitreg_7_out_5), .in7(sixteenbitreg_8_out_5), .out(rsOut), .sel(rs));
  Multiplexer #(.select(3), .width(16), .enable("false")) multiplexer_2 (
    .in0(sixteenbitreg_1_out_5), .in1(sixteenbitreg_2_out_5), .in2(sixteenbitreg_3_out_5),
    .in3(sixteenbitreg_4_out_5), .in4(sixteenbitreg_5_out_5), .in5(sixteenbitreg_6_out_5),
    .in6(sixteenbitreg_7_out_5), .in7(sixteenbitreg_8_out_5), .out(rtOut), .sel(rt));

  // Other names for the same wires on the sheet: Reset = in_3

  // Notes on the sheet:
  //   clock gated output
  //   r0 is never altered
endmodule

module fourBitEquator (
  input  [3:0] A,
  input  [3:0] B,
  output eq
);

  wire [3:0] xnor_1_out;

  assign xnor_1_out = ~(A ^ B);  // XNOR_Gate xnor_1, 4 bits wide
  and and_1 (eq, xnor_1_out[3], xnor_1_out[2], xnor_1_out[1], xnor_1_out[0]);
endmodule

module memory_latch (
  input  [15:0] address,
  input  WE,
  input  clk,
  input  [15:0] data_in,
  output [15:0] address_latched,
  output WE_latched,
  output OE_latched,
  output [15:0] data_in_latched
);

  wire d_ff_1_q;
  wire [15:0] register_1_q;

  Register #(.width(16), .trigger("falling")) register_1 (
    .D(address), .en(WE), .clk(clk), .Q(register_1_q));  // open: clr
  D_Flip_Flop #(.trigger("falling")) d_ff_1 (.D(WE), .clk(clk), .Q(d_ff_1_q));  // open: Qn, preset, reset
  Register #(.width(16), .trigger("falling")) register_2 (
    .D(data_in), .en(WE), .clk(clk), .Q(data_in_latched));  // open: clr
  Multiplexer #(.width(16), .enable("false")) multiplexer_1 (
    .in0(address), .in1(register_1_q), .out(address_latched), .sel(d_ff_1_q));
  and and_1 (WE_latched, clk, d_ff_1_q);
  not not_1 (OE_latched, WE_latched);
endmodule
