// Logisim project hw4_rishi.circ as structural Verilog: 3 circuits, main circuit main
module main (
);

  RegisterFile registerfile_1 ();  // open: Reset, clk, WE, Data_Input, rd, Rs, Rt, RtOut, RsOut
endmodule

module RegisterFile (
  input  Reset,
  input  clk,
  input  WE,
  input  [15:0] Data_Input,
  input  [2:0] rd,
  input  [2:0] Rt,
  input  [2:0] Rs,
  output [15:0] RtOut,
  output [15:0] RsOut
);

  wire clk_t, demultiplexer_1_out1, demultiplexer_1_out2, demultiplexer_1_out3, demultiplexer_1_out4,
       demultiplexer_1_out5, demultiplexer_1_out6, demultiplexer_1_out7;
  wire [15:0] register_1_out_5, register_2_out_5, register_3_out_5, register_4_out_5, register_5_out_5,
       register_6_out_5, register_7_out_5, register_8_out_5;

  and and_1 (clk_t, clk, WE);
  Demultiplexer #(.select(3), .enable("false")) demultiplexer_1 (
    .out1(demultiplexer_1_out1), .out2(demultiplexer_1_out2), .out3(demultiplexer_1_out3),
    .out4(demultiplexer_1_out4), .out5(demultiplexer_1_out5), .out6(demultiplexer_1_out6),
    .out7(demultiplexer_1_out7), .in(1'b1), .sel(rd));  // open: out0
  Register register_1 (.Reset(Reset), .clk(clk_t), .in_4(Data_Input), .out_5(register_1_out_5));  // open: enable
  Register register_2 (
    .Reset(Reset), .clk(clk_t), .enable(demultiplexer_1_out1), .in_4(Data_Input), .out_5(register_2_out_5));
  Register register_3 (
    .Reset(Reset), .clk(clk_t), .enable(demultiplexer_1_out2), .in_4(Data_Input), .out_5(register_3_out_5));
  Register register_4 (
    .Reset(Reset), .clk(clk_t), .enable(demultiplexer_1_out3), .in_4(Data_Input), .out_5(register_4_out_5));
  Register register_5 (
    .Reset(Reset), .clk(clk_t), .enable(demultiplexer_1_out4), .in_4(Data_Input), .out_5(register_5_out_5));
  Register register_6 (
    .Reset(Reset), .clk(clk_t), .enable(demultiplexer_1_out5), .in_4(Data_Input), .out_5(register_6_out_5));
  Register register_7 (
    .Reset(Reset), .clk(clk_t), .enable(demultiplexer_1_out6), .in_4(Data_Input), .out_5(register_7_out_5));
  Register register_8 (
    .Reset(Reset), .clk(clk_t), .enable(demultiplexer_1_out7), .in_4(Data_Input), .out_5(register_8_out_5));
  // Probe on register_1_out_5
  Multiplexer #(.select(3), .width(16), .enable("false")) multiplexer_1 (
    .in0(register_1_out_5), .in1(register_2_out_5), .in2(register_3_out_5), .in3(register_4_out_5),
    .in4(register_5_out_5), .in5(register_6_out_5), .in6(register_7_out_5), .in7(register_8_out_5),
    .out(RsOut), .sel(Rs));
  Multiplexer #(.select(3), .width(16), .enable("false")) multiplexer_2 (
    .in0(register_1_out_5), .in1(register_2_out_5), .in2(register_3_out_5), .in3(register_4_out_5),
    .in4(register_5_out_5), .in5(register_6_out_5), .in6(register_7_out_5), .in7(register_8_out_5),
    .out(RtOut), .sel(Rt));

  // Other names for the same wires on the sheet: DataIn[15:0] = Data_Input
endmodule

module Register (
  input  Reset,
  input  clk,
  input  enable,
  input  [15:0] in_4,
  output [15:0] out_5
);

  wire clk_t;

  and and_1 (clk_t, clk, enable);
  D_Flip_Flop d_ff_1 (.D(in_4[0]), .clk(clk_t), .Q(out_5[0]), .reset(Reset));  // open: Qn, preset
  D_Flip_Flop d_ff_2 (.D(in_4[1]), .clk(clk_t), .Q(out_5[1]), .reset(Reset));  // open: Qn, preset
  D_Flip_Flop d_ff_3 (.D(in_4[2]), .clk(clk_t), .Q(out_5[2]), .reset(Reset));  // open: Qn, preset
  D_Flip_Flop d_ff_4 (.D(in_4[3]), .clk(clk_t), .Q(out_5[3]), .reset(Reset));  // open: Qn, preset
  D_Flip_Flop d_ff_5 (.D(in_4[4]), .clk(clk_t), .Q(out_5[4]), .reset(Reset));  // open: Qn, preset
  D_Flip_Flop d_ff_6 (.D(in_4[5]), .clk(clk_t), .Q(out_5[5]), .reset(Reset));  // open: Qn, preset
  D_Flip_Flop d_ff_7 (.D(in_4[6]), .clk(clk_t), .Q(out_5[6]), .reset(Reset));  // open: Qn, preset
  D_Flip_Flop d_ff_8 (.D(in_4[7]), .clk(clk_t), .Q(out_5[7]), .reset(Reset));  // open: Qn, preset
  D_Flip_Flop d_ff_9 (.D(in_4[8]), .clk(clk_t), .Q(out_5[8]), .reset(Reset));  // open: Qn, preset
  D_Flip_Flop d_ff_10 (.D(in_4[9]), .clk(clk_t), .Q(out_5[9]), .reset(Reset));  // open: Qn, preset
  D_Flip_Flop d_ff_11 (.D(in_4[10]), .clk(clk_t), .Q(out_5[10]), .reset(Reset));  // open: Qn, preset
  D_Flip_Flop d_ff_12 (.D(in_4[11]), .clk(clk_t), .Q(out_5[11]), .reset(Reset));  // open: Qn, preset
  D_Flip_Flop d_ff_13 (.D(in_4[12]), .clk(clk_t), .Q(out_5[12]), .reset(Reset));  // open: Qn, preset
  D_Flip_Flop d_ff_14 (.D(in_4[13]), .clk(clk_t), .Q(out_5[13]), .reset(Reset));  // open: Qn, preset
  D_Flip_Flop d_ff_15 (.D(in_4[14]), .clk(clk_t), .Q(out_5[14]), .reset(Reset));  // open: Qn, preset
  D_Flip_Flop d_ff_16 (.D(in_4[15]), .clk(clk_t), .Q(out_5[15]), .reset(Reset));  // open: Qn, preset

  // Other names for the same wires on the sheet: bit0 = in_4[0]; bit1 = in_4[1]; bit2 = in_4[2]; bit3 = in_4[3];
  //   bit4 = in_4[4]; bit5 = in_4[5]; bit6 = in_4[6]; bit7 = in_4[7]; bit8 = in_4[8]; bit9 = in_4[9];
  //   bit10 = in_4[10]; bit11 = in_4[11]; bit12 = in_4[12]; bit13 = in_4[13]; bit14 = in_4[14]; bit15 = in_4[15];
  //   out0 = out_5[0]; out1 = out_5[1]; out2 = out_5[2]; out3 = out_5[3]; out4 = out_5[4]; out5 = out_5[5];
  //   out6 = out_5[6]; out7 = out_5[7]; out8 = out_5[8]; out9 = out_5[9]; out10 = out_5[10]; out11 = out_5[11];
  //   out12 = out_5[12]; out13 = out_5[13]; out14 = out_5[14]; out15 = out_5[15]

  // Notes on the sheet:
  //   Input
  //   Output
endmodule
